# Fritzing sketch controller (saved by Fritzing 0.9.3b)

parts:
  Part1 = Thumb Joystick
  Part2 = Arduino Pro Mini (3.3V)
  Part3 = NRF24L01+ Breakout Board
  BAT1 = BC9VPC [package=bc9vpc]

nets:
  GND: Part1.GND, Part2.GND, Part3.GND, BAT1.V-
  N1: Part1.HORZ, Part2.A0
  N2: Part1.VERT, Part2.A1
  N3: Part2.RAW, BAT1.V+
  VCC: Part2.VCC, Part3.VCC
  N4: Part2.SCK, Part3.SCK
  N5: Part2.MISO, Part3.MISO
  N6: Part2.MOSI, Part3.MOSI
  N7: Part2.D9, Part3.CS
  N8: Part2.D8, Part3.CE
